// Logisim project ToPlus9.circ as structural Verilog: 1 circuit, main circuit main
module main (
  input  [3:0] in_1,
  output [3:0] out_2,
  output Y0,
  output Y1,
  output Y2,
  output Y2_2
);

  wire not_1_out, not_2_out, not_3_out, not_4_out, or_1_out, or_2_out, or_3_out, or_4_out, or_5_out,
       or_6_out, or_7_out, or_8_out, or_9_out, or_10_out, or_11_out;

  // Probe on in_1
  not not_1 (not_1_out, in_1[3]);
  not not_2 (not_2_out, in_1[2]);
  not not_3 (not_3_out, in_1[1]);
  not not_4 (not_4_out, in_1[0]);
  or or_1 (or_1_out, not_2_out, not_3_out, not_4_out);
  or or_2 (or_2_out, not_3_out, not_2_out, not_4_out);
  or or_3 (or_3_out, in_1[2], in_1[1]);
  or or_4 (or_4_out, in_1[2], in_1[0]);
  or or_5 (or_5_out, not_1_out, not_2_out);
  or or_6 (or_6_out, not_1_out, not_3_out);
  or or_7 (or_7_out, not_1_out, in_1[0]);
  or or_8 (or_8_out, not_3_out, not_4_out);
  or or_9 (or_9_out, in_1[1], in_1[0]);
  or or_10 (or_10_out, not_1_out, not_2_out);
  or or_11 (or_11_out, not_1_out, not_3_out);
  and and_1 (out_2[3], not_1_out, or_1_out);
  and and_2 (out_2[2], or_2_out, or_3_out, or_4_out, not_1_out);
  and and_3 (out_2[0], or_10_out, or_11_out, not_4_out);
  and and_4 (out_2[1], or_5_out, or_6_out, or_7_out, or_8_out, or_9_out);
  // Probe on out_2

  assign Y0 = out_2[3];
  assign Y1 = out_2[2];
  assign Y2 = out_2[1];
  assign Y2_2 = out_2[0];

  // Notes on the sheet:
  //   X0
  //   X2
  //   X3
  //   X1
  //   !X0
  //   !X1
  //   !X3
  //   !X2
endmodule
